# Fritzing sketch lidar-pcb1 (saved by Fritzing 0.9.3b)
circuit board: 5cm x 5cm
breadboards: 1

parts:
  J1 = screw terminal, 6 pins
  Part1 = Arduino Nano (Rev3.0) (ICSP)
  Pololu_A1 = Pololu A4988 [package=SO16]
  J2 = screw terminal, 3 pins
  J3 = screw terminal, 4 pins
  C1 = Ceramic Capacitor [capacitance=4.7µF package="100 mil [THT, multilayer]"]
  C2 = Ceramic Capacitor [capacitance=100nF package="100 mil [THT, multilayer]"]  # not connected
  C3 = Electrolytic Capacitor [capacitance=1µF package="100 mil [THT, electrolytic]"]

nets (from the pcb view):
  N1: J1.pin5, Part1.A5
  N2: J1.pin6, Part1.A4
  N3: Part1.D0/RX, C3.+
  GND: Part1.GND, Pololu_A1.GND
  N4: Part1.D2, Pololu_A1.DIR
  N5: Part1.D3, Pololu_A1.STEP
  N6: Part1.D4, Pololu_A1.ENABLE
  5V: Part1.5V, Pololu_A1.VDD, Pololu_A1.1B, J2.pin3, J3.pin4
  N7: Pololu_A1.RESET, Pololu_A1.SLEEP
  N8: Pololu_A1.1A, J3.pin3
  N9: Pololu_A1.2A, J3.pin2
  N10: Pololu_A1.2B, J3.pin1
  N11: C1.0, C1.1
